# Fritzing sketch schematic (saved by Fritzing 0.9.3b)
breadboards: 1

parts:
  Componente1 = Arduino Uno (Rev3)
  SP1 = SPEAKER [package=pcb_mount_speaker]
  LED1 = LEDs [package=led10mm]
  LED2 = LEDs [package=led10mm]
  LED3 = LEDs [package=led10mm]
  LED4 = LEDs [package=led10mm]
  Q1 = Basic FET N-Channel [package="D2Pak [SMD]"]

nets:
  N1: Componente1.D9_PWM, Q1.Gate
  N2: Componente1.D10_PWM/SS, LED3.A
  N3: Componente1.D11_PWM/MOSI, LED4.A
  N4: Componente1.D12/MISO, LED2.A
  N5: Componente1.D13/SCK, LED1.A
  N6: Componente1.GND, LED1.C, LED2.C, LED3.C, LED4.C, Q1.source
  N7: Componente1.5V, SP1.-
  N8: SP1.+, Q1.drain
